// Logisim project lab1.circ as structural Verilog: 9 circuits, main circuit main
module main (
  input  in_1,
  input  [3:0] in_2,
  input  [7:0] in_3,
  input  [1:0] in_4,
  input  [1:0] in_5,
  input  in_6,
  input  in_7,
  input  in_8,
  input  in_9,
  input  in_10,
  input  [2:0] in_11,
  input  [1:0] in_12,
  output out_13,
  output [3:0] out_14,
  output [3:0] out_15,
  output [3:0] out_16,
  output [5:0] out_17,
  output [1:0] out_18,
  output [1:0] out_19,
  output [3:0] out_20,
  output [3:0] out_21,
  output [1:0] out_22,
  output [1:0] out_23,
  output [1:0] out_24,
  output [2:0] out_25,
  output [2:0] out_26
);

  wire button_1_out, nand_1_p1, nand_1_p4, nand_1_p7;
  wire [1:0] and_1_out;
  wire [2:2] or_1_out;

  Button button_1 (.out(button_1_out));
  // Probe on in_2
  // Probe on in_2
  assign and_1_out = in_4 & in_5;  // AND_Gate and_1, 2 bits wide
  or or_1 (or_1_out[2], in_6, in_7);
  // Probe on in_2
  // Probe on in_2
  // NAND_Gate nand_1: pin names not known; wires that end beside it: nand_1_p1, 1'b1, 1'b0, nand_1_p4, in_9, in_12, nand_1_p7
  // Probe on in_2
  LED led_1 (.in(button_1_out));
  // Probe on {or_1_out[2], and_1_out}
  assign out_25 = ~{or_1_out[2], and_1_out};  // NOT_Gate not_1, 3 bits wide

  assign in_10 = in_9;
  assign out_13 = in_1;
  assign out_14 = in_2;
  assign out_15 = in_3[3:0];
  assign out_16 = in_3[7:4];
  assign out_17 = in_3[7:2];
  assign out_18 = in_3[1:0];
  assign out_19 = in_3[3:2];
  assign out_20 = in_3[7:4];
  assign out_21 = in_3[3:0];
  assign out_22 = in_3[1:0];
  assign out_23 = in_3[5:4];
  assign out_24 = in_3[7:6];
  assign out_26 = in_11;

  // Notes on the sheet:
  //   王琛PB20111696 
endmodule

module Add (
  input  in_1,
  input  in_2,
  output Sum,
  output Cout
);

  xor xor_1 (Sum, in_1, in_2);
  and and_1 (Cout, in_1, in_2);

  // Notes on the sheet:
  //   王琛PB20111696 
endmodule

module Add_Test (
  input  in_1,
  input  in_2,
  input  in_3,
  output out_4,
  output out_5
);

  wire add_1_cout, add_1_sum, add_2_cout;

  Add add_1 (.in_1(in_1), .in_2(in_2), .Sum(add_1_sum), .Cout(add_1_cout));
  Add add_2 (.in_1(add_1_sum), .in_2(in_3), .Sum(out_4), .Cout(add_2_cout));
  or or_1 (out_5, add_2_cout, add_1_cout);

  // Notes on the sheet:
  //   王琛PB20111696 
endmodule

module Practice1 (
);

  DotMatrix #(.inputtype("row"), .matrixcols(16), .matrixrows(16)) dotmatrix_1 (
    .row0({16{1'b0}}), .row1(16'h7ffc), .row2(16'h100), .row3(16'h100), .row4(16'h100), .row5(16'h100),
    .row6(16'h100), .row7(16'h3ff8), .row8(16'h100), .row9(16'h100), .row10(16'h100), .row11(16'h100),
    .row12(16'h100), .row13(16'h100), .row14(16'hfffe), .row15({16{1'b0}}));
  DotMatrix #(.inputtype("row"), .matrixcols(16), .matrixrows(16)) dotmatrix_2 (
    .row0({16{1'b0}}), .row1(16'h7fc), .row2(16'hfc04), .row3(16'h24a4), .row4(16'h2110), .row5(16'h2208),
    .row6(16'h2040), .row7(16'hf840), .row8(16'h27fc), .row9(16'h2040), .row10(16'h20e0), .row11(16'h3950),
    .row12(16'he248), .row13(16'h4c46), .row14(16'h40), .row15(16'h40));
endmodule

module Practice2 (
);

  _7_Segment_Display u_7_segment_display_1 (
    .g(1'b1), .f(1'b0), .a(1'b1), .b(1'b1), .e(1'b1), .d(1'b1), .c(1'b0), .dp(1'b0));
  _7_Segment_Display u_7_segment_display_2 (
    .g(1'b0), .f(1'b1), .a(1'b1), .b(1'b1), .e(1'b1), .d(1'b1), .c(1'b1), .dp(1'b0));
  _7_Segment_Display u_7_segment_display_3 (
    .g(1'b0), .f(1'b0), .a(1'b0), .b(1'b1), .e(1'b0), .d(1'b0), .c(1'b1), .dp(1'b0));
  _7_Segment_Display u_7_segment_display_4 (
    .g(1'b0), .f(1'b0), .a(1'b0), .b(1'b1), .e(1'b0), .d(1'b0), .c(1'b1), .dp(1'b0));
  _7_Segment_Display u_7_segment_display_5 (
    .g(1'b0), .f(1'b0), .a(1'b0), .b(1'b1), .e(1'b0), .d(1'b0), .c(1'b1), .dp(1'b0));
  _7_Segment_Display u_7_segment_display_6 (
    .g(1'b1), .f(1'b1), .a(1'b1), .b(1'b0), .e(1'b1), .d(1'b1), .c(1'b1), .dp(1'b0));
  _7_Segment_Display u_7_segment_display_7 (
    .g(1'b1), .f(1'b1), .a(1'b1), .b(1'b1), .e(1'b0), .d(1'b1), .c(1'b1), .dp(1'b0));
  _7_Segment_Display u_7_segment_display_8 (
    .g(1'b1), .f(1'b1), .a(1'b1), .b(1'b0), .e(1'b1), .d(1'b1), .c(1'b1), .dp(1'b0));
endmodule

module AND (
  input  in_1,
  input  in_2,
  output out_3
);

  wire transistor_2_out;

  Transistor transistor_1 (.in(1'b0), .out(out_3), .gate(in_2));
  Transistor #(.\type ("n")) transistor_2 (.in(1'b1), .out(transistor_2_out), .gate(in_1));
  Transistor #(.\type ("n")) transistor_3 (.in(transistor_2_out), .out(out_3), .gate(in_2));
  Transistor transistor_4 (.in(1'b0), .out(out_3), .gate(in_1));

  // Notes on the sheet:
  //   王琛PB20111696 
endmodule

module OR (
  input  in_1,
  input  in_2,
  output out_3
);

  wire transistor_4_out;

  Transistor #(.\type ("n")) transistor_1 (.in(1'b1), .out(out_3), .gate(in_1));
  Transistor #(.\type ("n")) transistor_2 (.in(1'b1), .out(out_3), .gate(in_2));
  Transistor transistor_3 (.in(transistor_4_out), .out(out_3), .gate(in_2));
  Transistor transistor_4 (.in(1'b0), .out(transistor_4_out), .gate(in_1));

  // Notes on the sheet:
  //   王琛PB20111696 
endmodule

module NOT (
  input  in_1,
  output out_2
);

  Transistor transistor_1 (.in(1'b1), .out(out_2), .gate(in_1));
  Transistor #(.\type ("n")) transistor_2 (.in(1'b0), .out(out_2), .gate(in_1));

  // Notes on the sheet:
  //   王琛PB20111696 
endmodule

module Practice4 (
  input  in_1,
  input  in_2,
  input  in_3,
  input  in_4,
  input  in_5,
  input  in_6,
  input  in_7,
  input  in_8,
  input  in_9,
  input  in_10,
  input  in_11,
  input  in_12,
  input  in_13,
  output out_14,
  output out_15,
  output out_16
);

  wire and_1_out_3, and_2_out_3, and_3_out_3, and_4_out_3, and_5_out_3, and_6_out_3, and_7_out_3,
       and_8_out_3, and_9_out_3, and_10_out_3, and_11_out_3, and_12_out_3, and_13_out_3, and_14_out_3,
       not_1_out_2, not_2_out_2, not_3_out_2, or_2_out_3, or_3_out_3, or_4_out_3, or_5_out_3;

  NOT not_1 (.in_1(in_6), .out_2(not_1_out_2));
  AND and_1 (.in_1(in_8), .in_2(in_6), .out_3(and_1_out_3));
  AND and_2 (.in_1(in_9), .in_2(not_1_out_2), .out_3(and_2_out_3));
  OR or_1 (.in_1(and_1_out_3), .in_2(and_2_out_3), .out_3(out_15));
  NOT not_2 (.in_1(in_1), .out_2(not_2_out_2));
  AND and_3 (.in_1(in_2), .in_2(in_1), .out_3(and_3_out_3));
  AND and_4 (.in_1(in_4), .in_2(not_2_out_2), .out_3(and_4_out_3));
  AND and_5 (.in_1(in_5), .in_2(in_1), .out_3(and_5_out_3));
  AND and_6 (.in_1(in_7), .in_2(not_2_out_2), .out_3(and_6_out_3));
  AND and_7 (.in_1(in_10), .in_2(in_1), .out_3(and_7_out_3));
  AND and_8 (.in_1(in_11), .in_2(not_2_out_2), .out_3(and_8_out_3));
  AND and_9 (.in_1(in_12), .in_2(in_1), .out_3(and_9_out_3));
  AND and_10 (.in_1(in_13), .in_2(not_2_out_2), .out_3(and_10_out_3));
  OR or_2 (.in_1(and_3_out_3), .in_2(and_4_out_3), .out_3(or_2_out_3));
  OR or_3 (.in_1(and_5_out_3), .in_2(and_6_out_3), .out_3(or_3_out_3));
  OR or_4 (.in_1(and_7_out_3), .in_2(and_8_out_3), .out_3(or_4_out_3));
  OR or_5 (.in_1(and_9_out_3), .in_2(and_10_out_3), .out_3(or_5_out_3));
  NOT not_3 (.in_1(in_3), .out_2(not_3_out_2));
  AND and_11 (.in_1(or_2_out_3), .in_2(in_3), .out_3(and_11_out_3));
  AND and_12 (.in_1(or_3_out_3), .in_2(not_3_out_2), .out_3(and_12_out_3));
  AND and_13 (.in_1(or_4_out_3), .in_2(in_3), .out_3(and_13_out_3));
  AND and_14 (.in_1(or_5_out_3), .in_2(not_3_out_2), .out_3(and_14_out_3));
  OR or_6 (.in_1(and_11_out_3), .in_2(and_12_out_3), .out_3(out_14));
  OR or_7 (.in_1(and_13_out_3), .in_2(and_14_out_3), .out_3(out_16));

  // Notes on the sheet:
  //   王琛PB20111696 
endmodule
