// Logisim project lab2.circ as structural Verilog
module \真值表生成电路  (
  input  I4,
  input  I3,
  input  I2,
  input  I1,
  output O4,
  output O3,
  output O2,
  output O1
);

  wire and_2_out, not_3_out, not_4_out;

  not not_1 (O4, I2);
  and and_1 (O3, I2, I1);
  not not_2 (O2, I3);
  not not_3 (not_3_out, I1);
  not not_4 (not_4_out, I4);
  and and_2 (and_2_out, not_4_out, I2);
  or or_1 (O1, not_3_out, and_2_out, I3);
endmodule

module \表达式生成电路  (
  input  i7,
  input  i6,
  input  i5,
  input  i4,
  input  i3,
  input  i2,
  input  i1,
  input  i0,
  output y2,
  output y1,
  output y0
);

  wire and_1_out, and_2_out, and_3_out, and_4_out, and_5_out, and_6_out, and_7_out, and_8_out, and_9_out,
       not_1_out, not_2_out, not_3_out, not_4_out, not_5_out, not_6_out, not_7_out, not_8_out, not_9_out,
       not_10_out, not_11_out, not_12_out, not_13_out, not_14_out, not_15_out, not_16_out, not_17_out,
       not_18_out, not_19_out, not_20_out, not_21_out, not_22_out, not_23_out, not_24_out, not_25_out,
       not_26_out, not_27_out, not_28_out;

  not not_1 (not_1_out, i7);
  not not_2 (not_2_out, i7);
  not not_3 (not_3_out, i6);
  not not_4 (not_4_out, i7);
  not not_5 (not_5_out, i6);
  not not_6 (not_6_out, i5);
  not not_7 (not_7_out, i7);
  not not_8 (not_8_out, i7);
  not not_9 (not_9_out, i6);
  not not_10 (not_10_out, i5);
  not not_11 (not_11_out, i4);
  not not_12 (not_12_out, i7);
  not not_13 (not_13_out, i6);
  not not_14 (not_14_out, i5);
  not not_15 (not_15_out, i4);
  not not_16 (not_16_out, i3);
  not not_17 (not_17_out, i7);
  not not_18 (not_18_out, i6);
  not not_19 (not_19_out, i7);
  not not_20 (not_20_out, i6);
  not not_21 (not_21_out, i5);
  not not_22 (not_22_out, i4);
  not not_23 (not_23_out, i7);
  not not_24 (not_24_out, i6);
  not not_25 (not_25_out, i5);
  not not_26 (not_26_out, i4);
  not not_27 (not_27_out, i3);
  not not_28 (not_28_out, i2);
  and and_1 (and_1_out, not_1_out, i6);
  and and_2 (and_2_out, not_2_out, not_3_out, i5);
  and and_3 (and_3_out, not_4_out, not_5_out, not_6_out, i4);
  and and_4 (and_4_out, not_7_out, i6);
  and and_5 (and_5_out, not_8_out, not_9_out, not_10_out, not_11_out, i3);
  and and_6 (and_6_out, not_12_out, not_13_out, not_14_out, not_15_out, not_16_out, i2);
  and and_7 (and_7_out, not_17_out, not_18_out, i5);
  and and_8 (and_8_out, not_19_out, not_20_out, not_21_out, not_22_out, i3);
  and and_9 (and_9_out, not_23_out, not_24_out, not_25_out, not_26_out, not_27_out, not_28_out, i1);
  or or_1 (y2, i7, and_1_out, and_2_out, and_3_out);
  or or_2 (y1, i7, and_4_out, and_5_out, and_6_out);
  or or_3 (y0, i7, and_7_out, and_8_out, and_9_out);
endmodule

module \电路化简1  (
  input  i7,
  input  i6,
  input  i5,
  input  i4,
  input  i3,
  input  i2,
  input  i1,
  input  i0,
  output y2,
  output y1,
  output y0
);

  wire and_1_out, and_2_out, and_3_out, and_4_out, and_5_out, not_1_out, not_2_out, not_3_out, not_4_out,
       not_5_out, not_6_out, not_7_out, not_8_out, not_9_out, not_10_out;

  or or_1 (y2, i4, i5, i6, i7);
  not not_1 (not_1_out, i5);
  not not_2 (not_2_out, i4);
  and and_1 (and_1_out, not_1_out, not_2_out, i2);
  not not_3 (not_3_out, i5);
  not not_4 (not_4_out, i4);
  and and_2 (and_2_out, not_3_out, not_4_out, i3);
  not not_5 (not_5_out, i6);
  not not_6 (not_6_out, i4);
  not not_7 (not_7_out, i2);
  not not_8 (not_8_out, i6);
  not not_9 (not_9_out, i4);
  not not_10 (not_10_out, i6);
  or or_2 (y1, and_1_out, and_2_out, i6, i7);
  and and_3 (and_3_out, not_5_out, not_6_out, not_7_out, i1);
  and and_4 (and_4_out, not_8_out, not_9_out, i3);
  and and_5 (and_5_out, not_10_out, i5);
  or or_3 (y0, and_3_out, and_4_out, and_5_out, i7);
endmodule

module \电路化简2  (
  input  i7,
  input  i6,
  input  i5,
  input  i4,
  input  i3,
  input  i2,
  input  i1,
  input  i0,
  output y2,
  output y1,
  output y0
);

  wire not_1_out, not_2_out, not_3_out, not_4_out, not_5_out, or_2_out, or_3_out, or_4_out, or_5_out,
       or_6_out, or_7_out, or_8_out;

  or or_1 (y2, i7, i6, i5, i4);
  or or_2 (or_2_out, i7, i6, i3, i2);
  or or_3 (or_3_out, i7, i6, not_1_out);
  not not_1 (not_1_out, i4);
  or or_4 (or_4_out, i7, i6, not_2_out);
  not not_2 (not_2_out, i5);
  not not_3 (not_3_out, i2);
  not not_4 (not_4_out, i4);
  not not_5 (not_5_out, i6);
  and and_1 (y1, or_2_out, or_3_out, or_4_out);
  or or_5 (or_5_out, i7, i5, i3, i1);
  or or_6 (or_6_out, i7, i5, i3, not_3_out);
  or or_7 (or_7_out, i7, i5, not_4_out);
  or or_8 (or_8_out, i7, not_5_out);
  and and_2 (y0, or_5_out, or_6_out, or_7_out, or_8_out);
endmodule

module Practice1 (
  input  Ci1,
  input  Ai,
  input  Bi,
  output Si,
  output Ci
);

  wire and_1_out, and_2_out, and_3_out, and_4_out, and_5_out, and_6_out, and_7_out, not_1_out, not_2_out,
       not_3_out, not_4_out, not_5_out, not_6_out;

  not not_1 (not_1_out, Ci1);
  not not_2 (not_2_out, Ai);
  not not_3 (not_3_out, Ci1);
  not not_4 (not_4_out, Bi);
  not not_5 (not_5_out, Ai);
  not not_6 (not_6_out, Bi);
  and and_1 (and_1_out, Ai, Bi);
  and and_2 (and_2_out, Ci1, Bi);
  and and_3 (and_3_out, Ci1, Ai);
  and and_4 (and_4_out, not_1_out, not_2_out, Bi);
  and and_5 (and_5_out, not_3_out, Ai, not_4_out);
  and and_6 (and_6_out, Ci1, not_5_out, not_6_out);
  and and_7 (and_7_out, Ci1, Ai, Bi);
  or or_1 (Ci, and_1_out, and_2_out, and_3_out);
  or or_2 (Si, and_4_out, and_5_out, and_6_out, and_7_out);
endmodule

module Practice2 (
  input  G1,
  input  G2,
  input  G3,
  input  A2,
  input  A1,
  input  A0,
  output Y7,
  output Y6,
  output Y5,
  output Y4,
  output Y3,
  output Y2,
  output Y1,
  output Y0
);

  wire nand_1_out, nand_2_out, nand_3_out, nand_4_out, nand_5_out, nand_6_out, nand_7_out, nand_8_out,
       not_1_out, not_2_out, not_3_out, not_4_out, not_5_out, not_6_out, not_7_out, not_8_out, not_9_out,
       not_10_out, not_11_out, not_12_out, not_13_out, not_14_out, not_15_out, not_16_out, not_17_out,
       not_18_out, not_19_out, not_20_out, not_21_out, not_22_out, not_23_out, not_24_out, not_25_out,
       not_26_out, not_27_out, not_28_out;

  not not_1 (not_1_out, G2);
  not not_2 (not_2_out, G3);
  nand nand_1 (nand_1_out, A2, A1, A0);
  not not_3 (not_3_out, A0);
  not not_4 (not_4_out, A1);
  not not_5 (not_5_out, A1);
  not not_6 (not_6_out, A0);
  not not_7 (not_7_out, A2);
  not not_8 (not_8_out, A2);
  not not_9 (not_9_out, A0);
  not not_10 (not_10_out, A2);
  not not_11 (not_11_out, A1);
  not not_12 (not_12_out, A2);
  not not_13 (not_13_out, A1);
  not not_14 (not_14_out, A0);
  and and_1 (Y7, G1, not_1_out, not_2_out, nand_1_out);
  not not_15 (not_15_out, G2);
  not not_16 (not_16_out, G3);
  nand nand_2 (nand_2_out, A2, A1, not_3_out);
  not not_17 (not_17_out, G2);
  not not_18 (not_18_out, G3);
  nand nand_3 (nand_3_out, A2, not_4_out, A0);
  not not_19 (not_19_out, G2);
  not not_20 (not_20_out, G3);
  nand nand_4 (nand_4_out, A2, not_5_out, not_6_out);
  not not_21 (not_21_out, G2);
  not not_22 (not_22_out, G3);
  nand nand_5 (nand_5_out, not_7_out, A1, A0);
  not not_23 (not_23_out, G2);
  not not_24 (not_24_out, G3);
  nand nand_6 (nand_6_out, not_8_out, A1, not_9_out);
  not not_25 (not_25_out, G2);
  not not_26 (not_26_out, G3);
  nand nand_7 (nand_7_out, not_10_out, not_11_out, A0);
  not not_27 (not_27_out, G2);
  not not_28 (not_28_out, G3);
  nand nand_8 (nand_8_out, not_12_out, not_13_out, not_14_out);
  and and_2 (Y6, G1, not_15_out, not_16_out, nand_2_out);
  and and_3 (Y5, G1, not_17_out, not_18_out, nand_3_out);
  and and_4 (Y4, G1, not_19_out, not_20_out, nand_4_out);
  and and_5 (Y3, G1, not_21_out, not_22_out, nand_5_out);
  and and_6 (Y2, G1, not_23_out, not_24_out, nand_6_out);
  and and_7 (Y1, G1, not_25_out, not_26_out, nand_7_out);
  and and_8 (Y0, G1, not_27_out, not_28_out, nand_8_out);
endmodule

module Practice3 (
  input  sel,
  input  a,
  input  b,
  output out_4
);

  wire and_1_out, and_2_out, not_1_out;

  not not_1 (not_1_out, sel);
  and and_1 (and_1_out, a, sel);
  and and_2 (and_2_out, b, not_1_out);
  or or_1 (out_4, and_1_out, and_2_out);
endmodule

module Practice4 (
  input  sel1,
  input  sel0,
  input  d,
  input  b,
  input  c,
  input  a,
  output out_7
);

  wire practice3_1_out_4, practice3_2_out_4;

  Practice3 practice3_1 (.a(d), .b(b), .out_4(practice3_1_out_4), .sel(sel1));
  Practice3 practice3_2 (.a(c), .b(a), .out_4(practice3_2_out_4), .sel(sel1));
  Practice3 practice3_3 (.a(practice3_1_out_4), .b(practice3_2_out_4), .out_4(out_7), .sel(sel0));
endmodule

module Practice6 (
  input  a,
  input  b,
  input  c,
  output s1,
  output s2
);

  wire and_1_out, and_2_out, and_3_out, and_4_out, and_5_out, and_6_out, and_7_out, and_8_out, not_1_out,
       not_2_out, not_3_out, not_4_out, not_5_out, not_6_out, not_7_out, not_8_out, not_9_out, not_10_out,
       not_11_out, not_12_out;

  not not_1 (not_1_out, a);
  not not_2 (not_2_out, b);
  not not_3 (not_3_out, a);
  not not_4 (not_4_out, c);
  not not_5 (not_5_out, b);
  not not_6 (not_6_out, c);
  not not_7 (not_7_out, a);
  not not_8 (not_8_out, b);
  not not_9 (not_9_out, c);
  not not_10 (not_10_out, a);
  not not_11 (not_11_out, b);
  not not_12 (not_12_out, c);
  and and_1 (and_1_out, not_1_out, not_2_out, c);
  and and_2 (and_2_out, not_3_out, b, not_4_out);
  and and_3 (and_3_out, a, not_5_out, not_6_out);
  and and_4 (and_4_out, a, b, c);
  and and_5 (and_5_out, not_7_out, b, c);
  and and_6 (and_6_out, a, not_8_out, c);
  and and_7 (and_7_out, a, b, not_9_out);
  and and_8 (and_8_out, not_10_out, not_11_out, not_12_out);
  or or_1 (s1, and_1_out, and_2_out, and_3_out, and_4_out);
  or or_2 (s2, and_5_out, and_6_out, and_7_out, and_8_out);
endmodule
