// Logisim project lab3.circ as structural Verilog
module \双稳态电路  (
  input  in_1,
  input  in_2,
  output out_3,
  output out_4,
  output out_5,
  output out_6
);

  not not_1 (out_3, out_5);
  not not_2 (out_5, out_3);
  not not_3 (out_4, out_6);
  not not_4 (out_6, out_4);

  // Notes on the sheet:
  //   王琛 PB20111696
endmodule

module \或非SR锁存器  (
  input  R,
  input  S,
  output Q,
  output nQ
);

  nor nor_1 (Q, R, nQ);
  nor nor_2 (nQ, Q, S);

  // Notes on the sheet:
  //   王琛 PB20111696
endmodule

module \与非SR锁存器  (
  input  R,
  input  S,
  output Q,
  output nQ
);

  nand nand_1 (Q, R, nQ);
  nand nand_2 (nQ, Q, S);

  // Notes on the sheet:
  //   王琛 PB20111696
endmodule

module \D锁存器  (
  input  CLK,
  input  D,
  output Q,
  output nQ
);

  wire and_1_out, and_2_out, not_1_out;

  not not_1 (not_1_out, D);
  and and_1 (and_1_out, CLK, not_1_out);
  and and_2 (and_2_out, CLK, D);
  \或非SR锁存器  \u_或非sr锁存器_1  (.R(and_1_out), .S(and_2_out), .Q(Q), .nQ(nQ));

  // Notes on the sheet:
  //   王琛 PB20111696
endmodule

module \复位置0D锁存器  (
  input  CLK,
  input  D,
  input  RST,
  output Q,
  output nQ
);

  wire and_1_out, and_2_out, and_3_out, not_1_out, or_1_out;

  not not_1 (not_1_out, D);
  and and_1 (and_1_out, CLK, not_1_out);
  and and_2 (and_2_out, CLK, D);
  or or_1 (or_1_out, and_1_out, ~RST);  // OR_Gate
  and and_3 (and_3_out, and_2_out, RST);
  \或非SR锁存器  \u_或非sr锁存器_1  (.R(or_1_out), .S(and_3_out), .Q(Q), .nQ(nQ));

  // Notes on the sheet:
  //   王琛 PB20111696
endmodule

module \复位置1D锁存器  (
  input  CLK,
  input  D,
  input  RST,
  output Q,
  output nQ
);

  wire and_1_out, and_2_out, and_3_out, not_1_out, or_1_out;

  not not_1 (not_1_out, D);
  and and_1 (and_1_out, CLK, not_1_out);
  and and_2 (and_2_out, CLK, D);
  and and_3 (and_3_out, and_1_out, RST);
  or or_1 (or_1_out, and_2_out, ~RST);  // OR_Gate
  \或非SR锁存器  \u_或非sr锁存器_1  (.R(and_3_out), .S(or_1_out), .Q(Q), .nQ(nQ));

  // Notes on the sheet:
  //   王琛 PB20111696
endmodule

module \D触发器  (
  input  CLK,
  input  D,
  output Q,
  output nQ
);

  wire \d锁存器_1_q , not_1_out;

  not not_1 (not_1_out, CLK);
  \D锁存器  \d锁存器_1  (.CLK(not_1_out), .D(D), .Q(\d锁存器_1_q ));  // open: nQ
  \D锁存器  \d锁存器_2  (.CLK(CLK), .D(\d锁存器_1_q ), .Q(Q), .nQ(nQ));

  // Notes on the sheet:
  //   D1
  //   王琛 PB20111696
  //   D2
endmodule

module \同步复位置0D触发器  (
  input  D,
  input  nRST,
  output Q,
  output nQ
);

  wire and_1_out, CLK_out;

  Clock CLK (.out(CLK_out));
  and and_1 (and_1_out, D, nRST);
  \D触发器  \d触发器_1  (.D(and_1_out), .Q(Q), .nQ(nQ), .CLK(CLK_out));

  // Notes on the sheet:
  //   王琛 PB20111696
endmodule

module \异步复位置0D触发器  (
  input  CLK,
  input  D,
  input  RST,
  output Q,
  output nQ
);

  wire not_1_out, \复位置0d锁存器_1_q ;

  not not_1 (not_1_out, CLK);
  \复位置0D锁存器  \u_复位置0d锁存器_1  (.CLK(not_1_out), .D(D), .RST(RST), .Q(\复位置0d锁存器_1_q ));  // open: nQ
  \复位置0D锁存器  \u_复位置0d锁存器_2  (.CLK(CLK), .D(\复位置0d锁存器_1_q ), .RST(RST), .Q(Q), .nQ(nQ));

  // Notes on the sheet:
  //   D1
  //   王琛 PB20111696
  //   D2
endmodule

module \异步复位置1D触发器  (
  input  CLK,
  input  D,
  input  RST,
  output Q,
  output nQ
);

  wire not_1_out, \复位置1d锁存器_1_q ;

  not not_1 (not_1_out, CLK);
  \复位置1D锁存器  \u_复位置1d锁存器_1  (.CLK(not_1_out), .D(D), .RST(RST), .Q(\复位置1d锁存器_1_q ));  // open: nQ
  \复位置1D锁存器  \u_复位置1d锁存器_2  (.CLK(CLK), .D(\复位置1d锁存器_1_q ), .RST(RST), .Q(Q), .nQ(nQ));

  // Notes on the sheet:
  //   D1
  //   王琛 PB20111696
  //   D2
endmodule

module \同步复位置0寄存器  (
  input  [3:0] _0_IN,
  input  in_2,
  input  in_3,
  output [3:0] _0_OUT
);

  wire and_1_out, and_2_out, and_3_out, and_4_out;

  and and_1 (and_1_out, in_3, _0_IN[0]);
  and and_2 (and_2_out, in_3, _0_IN[1]);
  and and_3 (and_3_out, in_3, _0_IN[2]);
  and and_4 (and_4_out, in_3, _0_IN[3]);
  \D触发器  \d触发器_1  (.D(and_1_out), .Q(_0_OUT[0]), .CLK(in_2));  // open: nQ
  \D触发器  \d触发器_2  (.D(and_2_out), .Q(_0_OUT[1]), .CLK(in_2));  // open: nQ
  \D触发器  \d触发器_3  (.D(and_3_out), .Q(_0_OUT[2]), .CLK(in_2));  // open: nQ
  \D触发器  \d触发器_4  (.D(and_4_out), .Q(_0_OUT[3]), .CLK(in_2));  // open: nQ

  // Notes on the sheet:
  //   王琛 PB20111696
endmodule

module \异步复位置0寄存器  (
  input  [3:0] _0_IN,
  input  CLK,
  input  RST,
  output [3:0] _0_OUT
);

  \异步复位置0D触发器  \u_异步复位置0d触发器_1  (.CLK(CLK), .D(_0_IN[0]), .RST(RST), .Q(_0_OUT[0]));  // open: nQ
  \异步复位置0D触发器  \u_异步复位置0d触发器_2  (.CLK(CLK), .D(_0_IN[1]), .RST(RST), .Q(_0_OUT[1]));  // open: nQ
  \异步复位置0D触发器  \u_异步复位置0d触发器_3  (.CLK(CLK), .D(_0_IN[2]), .RST(RST), .Q(_0_OUT[2]));  // open: nQ
  \异步复位置0D触发器  \u_异步复位置0d触发器_4  (.CLK(CLK), .D(_0_IN[3]), .RST(RST), .Q(_0_OUT[3]));  // open: nQ

  // Notes on the sheet:
  //   王琛 PB20111696
endmodule

module \异步复位置9寄存器  (
  input  [3:0] _0_IN,
  input  CLK,
  input  RST,
  output [3:0] _0_OUT
);

  \异步复位置1D触发器  \u_异步复位置1d触发器_1  (.CLK(CLK), .D(_0_IN[0]), .RST(RST), .Q(_0_OUT[0]));  // open: nQ
  \异步复位置0D触发器  \u_异步复位置0d触发器_1  (.CLK(CLK), .D(_0_IN[1]), .RST(RST), .Q(_0_OUT[1]));  // open: nQ
  \异步复位置0D触发器  \u_异步复位置0d触发器_2  (.CLK(CLK), .D(_0_IN[2]), .RST(RST), .Q(_0_OUT[2]));  // open: nQ
  \异步复位置1D触发器  \u_异步复位置1d触发器_2  (.CLK(CLK), .D(_0_IN[3]), .RST(RST), .Q(_0_OUT[3]));  // open: nQ

  // Notes on the sheet:
  //   王琛 PB20111696
endmodule

module \同步复位0_15计数器  (
  input  in_1,
  output [3:0] out_2
);

  wire clock_1_out;
  wire [3:0] adder_1_out;

  Clock clock_1 (.out(clock_1_out));
  Adder #(.width(4)) adder_1 (.a(out_2), .b(4'b0001), .out(adder_1_out), .cin(1'b0));  // open: cout
  \同步复位置0寄存器  \u_同步复位置0寄存器_1  (._0_IN(adder_1_out), .in_2(clock_1_out), .in_3(in_1), ._0_OUT(out_2));

  // Notes on the sheet:
  //   王琛 PB20111696
endmodule

module \异步复位0_15计数器  (
  input  in_1,
  output [3:0] out_2
);

  wire clock_1_out;
  wire [3:0] adder_1_out;

  Clock clock_1 (.out(clock_1_out));
  Adder #(.width(4)) adder_1 (.a(out_2), .b(4'b0001), .out(adder_1_out), .cin(1'b0));  // open: cout
  \异步复位置0寄存器  \u_异步复位置0寄存器_1  (._0_IN(adder_1_out), .CLK(clock_1_out), .RST(in_1), ._0_OUT(out_2));

  // Notes on the sheet:
  //   王琛 PB20111696
endmodule

module \异步复位9_0计数器  (
  input  in_1,
  output [3:0] out_2
);

  wire and_1_out, and_2_out, clock_1_out;
  wire [3:0] subtractor_1_out;

  Clock clock_1 (.out(clock_1_out));
  Subtractor #(.width(4)) subtractor_1 (.a(out_2), .b(4'b0001), .out(subtractor_1_out), .bin(1'b0));  // open: bout
  and and_1 (and_1_out, in_1, ~and_2_out);  // AND_Gate
  \异步复位置9寄存器  \u_异步复位置9寄存器_1  (._0_IN(subtractor_1_out), .CLK(clock_1_out), .RST(and_1_out), ._0_OUT(out_2));
  and and_2 (and_2_out, out_2[0], out_2[1], out_2[2], out_2[3]);

  // Notes on the sheet:
  //   王琛 PB20111696
endmodule

module \高电平有效复位信号示例  (
  input  D,
  input  nRST,
  output Q,
  output nQ
);

  wire and_1_out, CLK_out;

  Clock CLK (.out(CLK_out));
  and and_1 (and_1_out, D, ~nRST);  // AND_Gate
  \D触发器  \d触发器_1  (.D(and_1_out), .Q(Q), .nQ(nQ), .CLK(CLK_out));

  // Notes on the sheet:
  //   王琛 PB20111696
endmodule
