// Logisim project lab6.circ as structural Verilog: 1 circuit, main circuit main
module main (
  input  \输入1 ,
  input  \输入2 ,
  input  a,
  input  b,
  output \输出1 ,
  output \输出2 ,
  output \输出3 ,
  output \引脚A ,
  output \引脚B 
);

  wire clk_out, d_ff_1_q, decoder_1_out1, decoder_1_out2, decoder_1_out3, decoder_2_out1, decoder_2_out2,
       decoder_2_out3, decoder_3_out1, decoder_3_out2, decoder_3_out3, multiplexer_2_out, ram_1_data;
  wire [0:0] multiplexer_1_out;

  Clock clk (.out(clk_out));
  Multiplexer #(.enable("false")) multiplexer_1 (.in0(\输出1 ), .in1(a), .out(multiplexer_1_out[0]), .sel(1'b0));
  RAM #(.addrWidth(2), .dataWidth(1)) ram_1 (
    .addr({b, multiplexer_1_out[0]}), .data(ram_1_data));  // open: sel, clk, ld, clr
  D_Flip_Flop d_ff_1 (.clk(clk_out), .D(ram_1_data), .Q(d_ff_1_q));  // open: Qn, preset, en, reset
  Multiplexer #(.enable("false")) multiplexer_2 (.in0(d_ff_1_q), .in1(ram_1_data), .out(multiplexer_2_out), .sel(1'b0));
  Decoder #(.select(2)) decoder_1 (
    .out1(decoder_1_out1), .out2(decoder_1_out2), .out3(decoder_1_out3), .sel(2'b11));  // open: out0, en
  assign \输出1  = decoder_1_out1 ? \输入1  : 1'bz;  // Controlled_Buffer controlled_buffer_1
  assign \输出1  = decoder_1_out2 ? \输入2  : 1'bz;  // Controlled_Buffer controlled_buffer_2
  assign \输出1  = decoder_1_out3 ? multiplexer_2_out : 1'bz;  // Controlled_Buffer controlled_buffer_3
  assign \输出2  = decoder_2_out1 ? \输入1  : 1'bz;  // Controlled_Buffer controlled_buffer_4
  assign \输出2  = decoder_2_out2 ? \输入2  : 1'bz;  // Controlled_Buffer controlled_buffer_5
  assign \输出2  = decoder_2_out3 ? multiplexer_2_out : 1'bz;  // Controlled_Buffer controlled_buffer_6
  Decoder #(.select(2)) decoder_2 (
    .out1(decoder_2_out1), .out2(decoder_2_out2), .out3(decoder_2_out3), .sel(2'b00));  // open: out0, en
  Decoder #(.select(2)) decoder_3 (
    .out1(decoder_3_out1), .out2(decoder_3_out2), .out3(decoder_3_out3), .sel(2'b11));  // open: out0, en
  assign \输出3  = decoder_3_out1 ? \输入1  : 1'bz;  // Controlled_Buffer controlled_buffer_7
  assign \输出3  = decoder_3_out2 ? \输入2  : 1'bz;  // Controlled_Buffer controlled_buffer_8
  assign \输出3  = decoder_3_out3 ? multiplexer_2_out : 1'bz;  // Controlled_Buffer controlled_buffer_9
  // Buffer buffer_1 has open pins: in=\引脚A , out=open
  assign \引脚A  = 1'b1 ? \输出2  : 1'bz;  // Controlled_Buffer controlled_buffer_10
  // Buffer buffer_2 has open pins: in=\引脚B , out=open
  assign \引脚B  = 1'b1 ? \输出3  : 1'bz;  // Controlled_Buffer controlled_buffer_11
endmodule
