// Logisim project lab8.circ as structural Verilog: 1 circuit, main circuit main
module main (
  input  sw,
  input  rst,
  output [3:0] out_3
);

  wire and_1_out, and_2_out, clk_out, d_ff_1_q, d_ff_2_q, or_1_out;
  wire [3:0] adder_1_out, multiplexer_1_out;

  Clock clk (.out(clk_out));
  D_Flip_Flop d_ff_1 (.clk(clk_out), .D(sw), .Q(d_ff_1_q));  // open: Qn, preset, en, reset
  D_Flip_Flop d_ff_2 (.clk(clk_out), .D(d_ff_1_q), .Q(d_ff_2_q));  // open: Qn, preset, en, reset
  and and_1 (and_1_out, ~d_ff_2_q, d_ff_1_q);  // AND_Gate
  and and_2 (and_2_out, d_ff_2_q, ~d_ff_1_q);  // AND_Gate
  or or_1 (or_1_out, and_1_out, and_2_out);
  Adder #(.width(4)) adder_1 (.a(out_3), .b(4'b0000), .out(adder_1_out), .cin(1'b1));  // open: cout
  Multiplexer #(.width(4), .enable("false")) multiplexer_1 (
    .in0(out_3), .in1(adder_1_out), .out(multiplexer_1_out), .sel(or_1_out));
  Register #(.width(4)) register_1 (.D(multiplexer_1_out), .en(1'b1), .Q(out_3), .clk(clk_out), .clr(rst));
endmodule
